# Fritzing sketch Pieper 0.8.5 (saved by Fritzing 0.9.3b)
breadboards: 1

parts:
  Bauteil1 = Arduino Nano (Rev3.0)
  S1 = Pushbutton [package="[THT]"]
  ZS-042_RTC1 = ZS-042 RTC Module
  LCD1 = TFT 1.8 inch 160x128 w SD
  LED1 = LED - 5mm [color="Red (633nm)" package="5 mm [THT]"]  # not connected
  R1 = Trimmer Potentiometer [maximum_resistance=10kΩ package=THT]

nets:
  N1: Bauteil1.D4, LCD1.pin_9
  N2: Bauteil1.D8, LCD1.pin4
  N3: Bauteil1.D9, LCD1.pin_5
  N4: Bauteil1.D10, LCD1.pin3
  N5: Bauteil1.D11/MOSI, LCD1.pin_6, LCD1.pin_10
  N6: Bauteil1.D12/MISO, LCD1.pin_11
  N7: S1.Pin_1, S1.Pin_2
  N8: S1.Pin_3, S1.Pin_4
  N9: ZS-042_RTC1.GND, LCD1.pin2
  N10: ZS-042_RTC1.VCC, LCD1.pin_1, R1.leg2
  N11: LCD1.pin_8, R1.wiper

custom parts:
  TFT 1.8 inch 160x128 w SD: This is a generic 1.8 tft spi lcd display available on ebay and others. The 1.8" display has 128x160 color pixels.
